# Fritzing sketch circuito (saved by Fritzing 0.9.3b)
breadboards: 1

parts:
  R1 = Resistor [tolerance=±5% resistance=220 package=THT]
  R2 = Resistor [tolerance=±5% resistance=220 package=THT]
  Componente1 = Arduino Nano (Rev3.0)
  LED1 = LED - 5mm [color="Red (633nm)" package="5 mm [THT]"]
  LED2 = LED - 5mm [color="Red (660nm)" package="5 mm [THT]"]
  U1 = ESP8266 WiFi Module [part_number=ESP8266]
  R3 = Resistor [tolerance=±5% resistance=220 package=THT]
  Q1 = NPN-Transistor [package="TO92 [THT]"]
  SG2 = Buzzer 12mm [package=buzzer-ccv-kit]
  R4 = Resistor [tolerance=±5% resistance=220 package=THT]
  LED3 = LED - 5mm [color="Red (660nm)" package="5 mm [THT]"]
  RELAY1 = CAR RELAY [part_number=NVF4-2 package=THT]
  Componente2 = RFID-RC522-v2
  R5 = Photocell (LDR) [package=THT]  # not connected
  S1 = Round Pushbutton  # not connected
  Componente3 = HC-SR501 Body Sensor Module  # not connected

nets:
  N1: R1.Pin_0, Componente1.D6
  N2: R1.Pin_1, LED2.anode
  N3: R2.Pin_0, Componente1.D7
  N4: R2.Pin_1, LED1.anode
  N5: Componente1.D2, U1.TXD
  N6: Componente1.D3, U1.RXD
  N7: Componente1.D4, R3.Pin_0
  N8: Componente1.D5, SG2.1
  N9: Componente1.D8, R4.Pin_0
  N10: Componente1.D9, Componente2.RST
  N11: Componente1.D10, Componente2.SDA
  N12: Componente1.D11/MOSI, Componente2.MOSI
  N13: Componente1.D12/MISO, Componente2.MISO
  GND: Componente1.GND, LED1.cathode, LED2.cathode, U1.GND, Q1.E, SG2.2, LED3.cathode, Componente2.GND
  N14: Componente1.D13/SCK, Componente2.SCK
  3.3V: U1.VCC, U1.RST, Componente2.3.3V
  N15: R3.Pin_1, Q1.B
  N16: Q1.C, RELAY1.86
  N17: R4.Pin_1, LED3.anode
  12V: RELAY1.85, RELAY1.87

custom parts:
  ESP8266 WiFi Module: Generic WiFi Module based on the ESP8266 with onboard PCB antenna and UART communications
  RFID-RC522-v2: A simple China made RFID-RC522 Reader; do check the pin labels, as this is a MFRC522 based clone.
  HC-SR501 Body Sensor Module: Pyroelectric Infrared PIR Motion Sensor Detector Module
